# Fritzing sketch LMBoard (saved by Fritzing 0.9.1b)
circuit board: 6.32575cm x 2.87852cm
breadboards: 3

parts:
  IN = double row male pin header, 10 pins [form="♂ (male)"]
  R1 = Resistor [tolerance=±5% resistance=10k package=THT]
  R2 = Resistor [tolerance=±5% resistance=2k package=THT]
  U1 = Packages: [package=dil28-3]
  OUT = double row male pin header, 10 pins [form="♂ (male)"]
  LED1 = female pin header, 4 pins [form="♀ (female)"]
  LED2 = female pin header, 4 pins [form="♀ (female)"]
  LED3 = female pin header, 4 pins [form="♀ (female)"]
  LED4 = female pin header, 4 pins [form="♀ (female)"]
  LED5 = female pin header, 4 pins [form="♀ (female)"]
  Composant1 = Arduino Pro Mini v13

nets:
  GND: IN.pin1, IN.pin10, R2.Pin_0, U1.GND, U1.VPRG, OUT.pin1, OUT.pin10, Composant1.GND
  VCC: IN.pin2, IN.pin9, R1.Pin_0, U1.DCPRG, U1.VCC, OUT.pin2, OUT.pin9, LED1.pin3, LED2.pin3, LED3.pin3, LED4.pin3, LED5.pin3, Composant1.VCC
  N1: IN.pin3, IN.pin8, U1.GSCLK, OUT.pin3, OUT.pin8, Composant1.D3_PWM
  N2: IN.pin4, U1.XLAT, OUT.pin4, Composant1.D9_PWM
  N3: IN.pin5, R1.Pin_1, U1.BLANK, OUT.pin5, Composant1.D10_PWM/SS
  N4: IN.pin6, U1.SIN, Composant1.D11_PWM/MOSI
  N5: IN.pin7, U1.SCLK, OUT.pin7, Composant1.D13/SCK
  N6: R2.Pin_1, U1.IREF
  N7: U1.OUT1, LED1.pin2
  N8: U1.OUT2, LED1.pin4
  N9: U1.OUT3, LED2.pin1
  N10: U1.OUT4, LED2.pin2
  N11: U1.OUT5, LED2.pin4
  N12: U1.OUT6, LED3.pin1
  N13: U1.OUT7, LED3.pin2
  N14: U1.OUT8, LED3.pin4
  N15: U1.OUT9, LED4.pin1
  N16: U1.OUT10, LED4.pin2
  N17: U1.OUT11, LED4.pin4
  N18: U1.OUT12, LED5.pin1
  N19: U1.OUT13, LED5.pin2
  N20: U1.OUT14, LED5.pin4
  N21: U1.SOUT, OUT.pin6
  N22: U1.OUT0, LED1.pin1

notes:
  LEDMeter v1.0
  By : 40Thoughts
  email : 40thoughts@gmail.com
  website : www.stuffwedo.io
